# Fritzing sketch schematicDiagram (saved by Fritzing 0.9.3b)
breadboards: 1

parts:
  Microcontroller = Arduino Uno (Rev3) - ICSP
  BUZZER = Piezo Speaker
  RELAY = 1 chan 5v relay module
  12V_POWER_SUPPLY = DC Power [voltage=5]
  LED_LIGHT = LED - 5mm [color="Red (633nm)" package="5 mm [THT]"]
  IRF520_MOSFET = IFR520 MOS module [package=THT]
  POTENTIOMETER = POT [package=pot_mammoth]
  S1 = SPST Switch [package=r_sw_th]

nets:
  N1: Microcontroller.5V, RELAY.pin_1
  GND: Microcontroller.GND, BUZZER.pin2, RELAY.pin_2, 12V_POWER_SUPPLY.V-, LED_LIGHT.cathode, IRF520_MOSFET.GND, IRF520_MOSFET.V-, POTENTIOMETER.E
  N2: Microcontroller.D3_PWM, IRF520_MOSFET.SIG
  N3: Microcontroller.D4, BUZZER.pin1
  N4: Microcontroller.D6_PWM, RELAY.pin_3
  N5: RELAY.pin_4, 12V_POWER_SUPPLY.V+, IRF520_MOSFET.VIN
  N6: RELAY.pin_5, POTENTIOMETER.A
  N7: LED_LIGHT.anode, S1.P
  N8: IRF520_MOSFET.V+, S1.S
  N9: POTENTIOMETER.S, S1.O

custom parts:
  1 chan 5v relay module: 1 Channel 5V Relay Module Board Shield with Optocoupler Support High and Low Level Trigger for Arduino.
